// Logisim project branch-comp.circ as structural Verilog: 1 circuit, main circuit branch_comp
module branch_comp (
  input  [31:0] BrData1,
  input  [31:0] BrData2,
  input  BrUn,
  output BrEq,
  output BrLt
);

  wire [31:0] multiplexer_1_out, xor_1_out, xor_2_out;

  Multiplexer #(.enable("false"), .width(32)) multiplexer_1 (
    .in0(32'h80000000), .in1({32{1'b0}}), .out(multiplexer_1_out), .sel(BrUn));
  assign xor_1_out = BrData1 ^ multiplexer_1_out;  // XOR_Gate xor_1, 32 bits wide
  assign xor_2_out = BrData2 ^ multiplexer_1_out;  // XOR_Gate xor_2, 32 bits wide
  Comparator #(.width(32)) comparator_1 (.a(xor_1_out), .b(xor_2_out), .eq(BrEq), .lt(BrLt));  // open: gt

  // Notes on the sheet:
  //   INPUTS to your circuit
  //   DON'T CHANGE THE LOCATIONS OF THE INPUTS AND OUTPUTS!
  //   OUTPUT from your circuit
endmodule
