// Logisim project imm-gen.circ as structural Verilog: 1 circuit, main circuit imm_gen
module imm_gen (
  input  [31:0] Instruction,
  input  [2:0] ImmSel,
  output [31:0] Immediate
);

  wire [31:11] I_Type, S_Type;
  wire [31:12] B_Type;

  assign B_Type = {{19{Instruction[31]}}, Instruction[31]};  // Bit_Extender bit_extender_1
  assign S_Type = {{20{Instruction[31]}}, Instruction[31]};  // Bit_Extender bit_extender_2
  assign I_Type = {{20{Instruction[31]}}, Instruction[31]};  // Bit_Extender bit_extender_3
  Multiplexer #(.enable("false"), .select(3), .width(32)) multiplexer_1 (
    .in0({I_Type, Instruction[30:20]}), .in1({S_Type, Instruction[30:25], Instruction[11:7]}),
    .in2({B_Type, Instruction[7], Instruction[30:25], Instruction[11:8], 1'b0}), .out(Immediate), .sel(ImmSel));  // open: in3, in4, in5, in6, in7

  // Other names for the same wires on the sheet: I_Type[10:0] = Instruction[30:20];
  //   B_Type[11:1] = {Instruction[7], Instruction[30:25], Instruction[11:8]};
  //   S_Type[10:0] = {Instruction[30:25], Instruction[11:7]}

  // Notes on the sheet:
  //   INPUTS to your circuit
  //   DON'T CHANGE THE LOCATIONS OF THE INPUTS AND OUTPUTS!
  //   OUTPUT from your circuit
endmodule
